// Logisim project digitalproject.circ as structural Verilog: 10 circuits, main circuit CPU
module CPU (
);

  wire CF, Clear_out, ClearRegs_out, Clock, CompSignal, InstRead, MemRead, MemWrite, PCRead, PCSelect,
       PCWrite, RegWrite, ZF;
  wire [1:0] ALUControl;
  wire [2:0] multiplexer_2_out, multiplexer_4_out, ReadReg1, ReadReg2, writeReg;
  wire [8:0] Address9;
  wire [11:0] multiplexer_1_out, pc_1_out_6, pc_1_out_7;
  wire [11:9] Address12;
  wire [15:0] ALUResult, Data1, Data2, DataOut, multiplexer_3_out;
  wire [15:12] rom_1_data;

  Clock clock_1 (.out(Clock));
  COMPInstruction compinstruction_1 (
    .OP1(Data1), .OP2(Data2), .clock(Clock), .ZF(ZF), .CF(CF), .CompSignal(CompSignal));
  PC pc_1 (
    .Address12({Address12, Address9}), .Clr(Clear_out), .Enable(PCWrite), .Clock(Clock), .out_6(pc_1_out_6),
    .PcSelect(PCSelect), .out_7(pc_1_out_7));
  RAM #(.addrWidth(9), .dataWidth(16), .bus("separate")) ram_1 (
    .addr(Address9), .din(Data1), .data(DataOut), .str(MemWrite), .sel(1'b1), .clk(Clock), .ld(MemRead));  // open: clr
  Button Clear (.out(Clear_out));
  Multiplexer #(.width(12)) multiplexer_1 (
    .in0(pc_1_out_7), .in1(pc_1_out_6), .out(multiplexer_1_out), .sel(PCRead));  // open: en
  Multiplexer #(.width(3)) multiplexer_2 (
    .in0(writeReg), .in1(ReadReg1), .out(multiplexer_2_out), .sel(MemRead));  // open: en
  ROM #(.addrWidth(12), .dataWidth(16)) rom_1 (
    .addr(multiplexer_1_out), .data({rom_1_data, Address12, Address9}), .sel(1'b1));
  Multiplexer #(.width(16)) multiplexer_3 (
    .in0(ALUResult), .in1(DataOut), .out(multiplexer_3_out), .sel(MemRead));  // open: en
  Multiplexer #(.width(3)) multiplexer_4 (
    .in0(multiplexer_2_out), .in1(ReadReg2), .out(multiplexer_4_out), .sel(ALUControl[1]));  // open: en
  RegisterFile registerfile_1 (
    .WriteData(multiplexer_3_out), .ReadReg1(ReadReg1), .ReadReg2(ReadReg2),
    .WriteRegister(multiplexer_4_out), .writeReg(RegWrite), .Data2(Data2), .Data1(Data1),
    .Clear(ClearRegs_out), .in_6(Clock));
  ControlUnit controlunit_1 (
    .Instruction({rom_1_data, Address12, Address9}), .PCWrite(PCWrite), .MemWrite(MemWrite),
    .MemRead(MemRead), .RegWrite(RegWrite), .ZF(ZF), .CF(CF), .PcSelect(PCSelect), .WriteReg(writeReg),
    .ReadReg2(ReadReg2), .ReadReg1(ReadReg1), .CompSignal(CompSignal), .ALUControl(ALUControl),
    .InstRead(InstRead), .PcRead(PCRead), .in_2(Clock));
  Button ClearRegs (.out(ClearRegs_out));
  ALU alu_1 (.SRC1(Data1), .SRC2(Data2), .IMM6(Address9[5:0]), .Output(ALUResult), .ALUControl(ALUControl));

  // Other names for the same wires on the sheet: Address12[8:0] = Address9; IMM6[5:0] = Address9[5:0]

  // Notes on the sheet:
  //   Data Memory
  //   Instruction Memory
  //   contents of rom_1 (hex, n*v repeats v):
  //   e001 e202 e403 e604 e805 ea06 ec07 ee08 a003 7540 b002 8ffe 7940 9006 25a0 3280 6746 52bc 8ffa c003
  //   f607 8002 dffe
endmodule

module RegisterFile (
  input  [15:0] WriteData,
  input  [2:0] WriteRegister,
  input  [2:0] ReadReg1,
  input  [2:0] ReadReg2,
  input  writeReg,
  input  in_6,
  input  Clear,
  output [15:0] Data1,
  output [15:0] Data2
);

  wire and_1_out, and_2_out, and_3_out, and_4_out, and_5_out, and_6_out, and_7_out, and_8_out,
       decoder_1_out0, decoder_1_out1, decoder_1_out2, decoder_1_out3, decoder_1_out4, decoder_1_out5,
       decoder_1_out6, decoder_1_out7;
  wire [15:0] register_1_q, register_2_q, register_3_q, register_4_q, register_5_q, register_6_q,
       register_7_q, register_8_q;

  Decoder #(.select(3), .enable("false")) decoder_1 (
    .out0(decoder_1_out0), .out1(decoder_1_out1), .out2(decoder_1_out2), .out3(decoder_1_out3),
    .out4(decoder_1_out4), .out5(decoder_1_out5), .out6(decoder_1_out6), .out7(decoder_1_out7),
    .sel(WriteRegister));
  and and_1 (and_1_out, decoder_1_out0, writeReg);
  and and_2 (and_2_out, decoder_1_out1, writeReg);
  and and_3 (and_3_out, decoder_1_out2, writeReg);
  and and_4 (and_4_out, decoder_1_out3, writeReg);
  and and_5 (and_5_out, decoder_1_out4, writeReg);
  and and_6 (and_6_out, decoder_1_out5, writeReg);
  and and_7 (and_7_out, decoder_1_out6, writeReg);
  and and_8 (and_8_out, decoder_1_out7, writeReg);
  Register #(.width(16)) register_1 (.D(WriteData), .en(and_1_out), .Q(register_1_q), .clk(in_6), .clr(Clear));
  Register #(.width(16)) register_2 (.D(WriteData), .en(and_2_out), .Q(register_2_q), .clk(in_6), .clr(Clear));
  Register #(.width(16)) register_3 (.D(WriteData), .en(and_3_out), .Q(register_3_q), .clk(in_6), .clr(Clear));
  Register #(.width(16)) register_4 (.D(WriteData), .en(and_4_out), .Q(register_4_q), .clk(in_6), .clr(Clear));
  Register #(.width(16)) register_5 (.D(WriteData), .en(and_5_out), .Q(register_5_q), .clk(in_6), .clr(Clear));
  Register #(.width(16)) register_6 (.D(WriteData), .en(and_6_out), .Q(register_6_q), .clk(in_6), .clr(Clear));
  Register #(.width(16)) register_7 (.D(WriteData), .en(and_7_out), .Q(register_7_q), .clk(in_6), .clr(Clear));
  Register #(.width(16)) register_8 (.D(WriteData), .en(and_8_out), .Q(register_8_q), .clk(in_6), .clr(Clear));
  Multiplexer #(.select(3), .width(16)) multiplexer_1 (
    .in0(register_1_q), .in1(register_2_q), .in2(register_3_q), .in3(register_4_q), .in4(register_5_q),
    .in5(register_6_q), .in6(register_7_q), .in7(register_8_q), .out(Data1), .sel(ReadReg1));  // open: en
  Multiplexer #(.select(3), .width(16)) multiplexer_2 (
    .in0(register_1_q), .in1(register_2_q), .in2(register_3_q), .in3(register_4_q), .in4(register_5_q),
    .in5(register_6_q), .in6(register_7_q), .in7(register_8_q), .out(Data2), .sel(ReadReg2));  // open: en
endmodule

// FA
module FullAdder (
  input  CarryIn,
  input  B,
  input  A,
  output SUM,
  output CarryOut
);

  wire and_1_out, and_2_out, and_3_out;

  and and_1 (and_1_out, CarryIn, B);
  and and_2 (and_2_out, CarryIn, A);
  and and_3 (and_3_out, B, A);
  xor xor_1 (SUM, CarryIn, B, A);
  or or_1 (CarryOut, and_1_out, and_2_out, and_3_out);
endmodule

module Adder (
  input  [15:0] InputA,
  input  [15:0] InputB,
  output OverFlow,
  output [15:0] Output
);

  wire fulladder_2_carryout, fulladder_3_carryout, fulladder_4_carryout, fulladder_5_carryout,
       fulladder_6_carryout, fulladder_7_carryout, fulladder_8_carryout, fulladder_9_carryout,
       fulladder_10_carryout, fulladder_11_carryout, fulladder_12_carryout, fulladder_13_carryout,
       fulladder_14_carryout, fulladder_15_carryout, fulladder_16_carryout;

  FullAdder fulladder_1 (
    .CarryIn(fulladder_2_carryout), .B(InputA[15]), .A(InputB[15]), .SUM(Output[15]), .CarryOut(OverFlow));
  FullAdder fulladder_2 (
    .CarryIn(fulladder_3_carryout), .B(InputA[14]), .A(InputB[14]), .SUM(Output[14]),
    .CarryOut(fulladder_2_carryout));
  FullAdder fulladder_3 (
    .CarryIn(fulladder_4_carryout), .B(InputA[13]), .A(InputB[13]), .SUM(Output[13]),
    .CarryOut(fulladder_3_carryout));
  FullAdder fulladder_4 (
    .CarryIn(fulladder_5_carryout), .B(InputA[12]), .A(InputB[12]), .SUM(Output[12]),
    .CarryOut(fulladder_4_carryout));
  FullAdder fulladder_5 (
    .CarryIn(fulladder_6_carryout), .B(InputA[11]), .A(InputB[11]), .SUM(Output[11]),
    .CarryOut(fulladder_5_carryout));
  FullAdder fulladder_6 (
    .CarryIn(fulladder_7_carryout), .B(InputA[10]), .A(InputB[10]), .SUM(Output[10]),
    .CarryOut(fulladder_6_carryout));
  FullAdder fulladder_7 (
    .CarryIn(fulladder_8_carryout), .B(InputA[9]), .A(InputB[9]), .SUM(Output[9]),
    .CarryOut(fulladder_7_carryout));
  FullAdder fulladder_8 (
    .CarryIn(fulladder_9_carryout), .B(InputA[8]), .A(InputB[8]), .SUM(Output[8]),
    .CarryOut(fulladder_8_carryout));
  FullAdder fulladder_9 (
    .CarryIn(fulladder_10_carryout), .B(InputA[7]), .A(InputB[7]), .SUM(Output[7]),
    .CarryOut(fulladder_9_carryout));
  FullAdder fulladder_10 (
    .CarryIn(fulladder_11_carryout), .B(InputA[6]), .A(InputB[6]), .SUM(Output[6]),
    .CarryOut(fulladder_10_carryout));
  FullAdder fulladder_11 (
    .CarryIn(fulladder_12_carryout), .B(InputA[5]), .A(InputB[5]), .SUM(Output[5]),
    .CarryOut(fulladder_11_carryout));
  FullAdder fulladder_12 (
    .CarryIn(fulladder_13_carryout), .B(InputA[4]), .A(InputB[4]), .SUM(Output[4]),
    .CarryOut(fulladder_12_carryout));
  FullAdder fulladder_13 (
    .CarryIn(fulladder_14_carryout), .B(InputA[3]), .A(InputB[3]), .SUM(Output[3]),
    .CarryOut(fulladder_13_carryout));
  FullAdder fulladder_14 (
    .CarryIn(fulladder_15_carryout), .B(InputA[2]), .A(InputB[2]), .SUM(Output[2]),
    .CarryOut(fulladder_14_carryout));
  FullAdder fulladder_15 (
    .CarryIn(fulladder_16_carryout), .B(InputA[1]), .A(InputB[1]), .SUM(Output[1]),
    .CarryOut(fulladder_15_carryout));
  FullAdder fulladder_16 (
    .CarryIn(1'b0), .B(InputA[0]), .A(InputB[0]), .SUM(Output[0]), .CarryOut(fulladder_16_carryout));
endmodule

module ALU (
  input  [15:0] SRC1,
  input  [15:0] SRC2,
  input  [5:0] IMM6,
  input  [1:0] ALUControl,
  output [15:0] Output
);

  wire [15:0] adder_1_output, and_1_out, multiplexer_1_out;

  Multiplexer #(.width(16)) multiplexer_1 (
    .in0(SRC2), .in1({{11{IMM6[5]}}, IMM6[4:0]}), .out(multiplexer_1_out), .sel(ALUControl[1]));  // open: en
  assign and_1_out = SRC1 & multiplexer_1_out;  // AND_Gate and_1, 16 bits wide
  Adder adder_1 (.InputA(SRC1), .InputB(multiplexer_1_out), .Output(adder_1_output));  // open: OverFlow
  Multiplexer #(.width(16)) multiplexer_2 (
    .in0(and_1_out), .in1(adder_1_output), .out(Output), .sel(ALUControl[0]));  // open: en
endmodule

module PC (
  input  [11:0] Address12,
  input  PcSelect,
  input  Enable,
  input  Clr,
  input  Clock,
  output [11:0] out_6,
  output [11:0] out_7
);

  wire [11:0] multiplexer_1_out;
  wire [15:0] adder_1_output, bit_extender_1_out, register_1_q;

  Multiplexer #(.width(12)) multiplexer_1 (
    .in0(12'h1), .in1(Address12), .out(multiplexer_1_out), .sel(PcSelect));  // open: en
  assign bit_extender_1_out = {{4{multiplexer_1_out[11]}}, multiplexer_1_out};  // Bit_Extender bit_extender_1
  Adder adder_1 (.InputA(bit_extender_1_out), .InputB(register_1_q), .Output(adder_1_output));  // open: OverFlow
  Register #(.width(16)) register_1 (.D(adder_1_output), .en(Enable), .Q(register_1_q), .clk(Clock), .clr(Clr));
  Bit_Extender #(.in_width(16), .out_width(12)) bit_extender_2 (.in(register_1_q), .out(out_6));

  assign out_7 = out_6;

  // Notes on the sheet:
  //   counter++
endmodule

module FullComparator (
  input  Input1,
  input  Input2,
  input  great_in,
  input  less_in,
  input  equal_in,
  output great_out,
  output less_out,
  output equal_out
);

  wire and_1_out, and_2_out, xnor_1_out;

  and and_1 (and_1_out, Input1, equal_in, ~Input2);  // AND_Gate
  and and_2 (and_2_out, Input2, equal_in, ~Input1);  // AND_Gate
  xnor xnor_1 (xnor_1_out, Input2, Input1);
  or or_1 (great_out, and_1_out, great_in);
  or or_2 (less_out, and_2_out, less_in);
  and and_3 (equal_out, xnor_1_out, equal_in);
endmodule

module Comparator (
  input  [15:0] in_1,
  input  [15:0] in_2,
  output GreaterThan,
  output LessThan,
  output Equal
);

  wire fullcomparator_1_equal_out, fullcomparator_1_great_out, fullcomparator_1_less_out,
       fullcomparator_2_equal_out, fullcomparator_2_great_out, fullcomparator_2_less_out,
       fullcomparator_3_equal_out, fullcomparator_3_great_out, fullcomparator_3_less_out,
       fullcomparator_4_equal_out, fullcomparator_4_great_out, fullcomparator_4_less_out,
       fullcomparator_5_equal_out, fullcomparator_5_great_out, fullcomparator_5_less_out,
       fullcomparator_6_equal_out, fullcomparator_6_great_out, fullcomparator_6_less_out,
       fullcomparator_7_equal_out, fullcomparator_7_great_out, fullcomparator_7_less_out,
       fullcomparator_8_equal_out, fullcomparator_8_great_out, fullcomparator_8_less_out,
       fullcomparator_9_equal_out, fullcomparator_9_great_out, fullcomparator_9_less_out,
       fullcomparator_10_equal_out, fullcomparator_10_great_out, fullcomparator_10_less_out,
       fullcomparator_11_equal_out, fullcomparator_11_great_out, fullcomparator_11_less_out,
       fullcomparator_12_equal_out, fullcomparator_12_great_out, fullcomparator_12_less_out,
       fullcomparator_13_equal_out, fullcomparator_13_great_out, fullcomparator_13_less_out,
       fullcomparator_14_equal_out, fullcomparator_14_great_out, fullcomparator_14_less_out,
       fullcomparator_15_equal_out, fullcomparator_15_great_out, fullcomparator_15_less_out;

  FullComparator fullcomparator_1 (
    .Input1(in_1[15]), .Input2(in_2[15]), .great_in(1'b0), .less_in(1'b0), .equal_in(1'b1),
    .great_out(fullcomparator_1_great_out), .less_out(fullcomparator_1_less_out),
    .equal_out(fullcomparator_1_equal_out));
  FullComparator fullcomparator_2 (
    .Input1(in_1[14]), .Input2(in_2[14]), .great_in(fullcomparator_1_great_out),
    .less_in(fullcomparator_1_less_out), .equal_in(fullcomparator_1_equal_out),
    .great_out(fullcomparator_2_great_out), .less_out(fullcomparator_2_less_out),
    .equal_out(fullcomparator_2_equal_out));
  FullComparator fullcomparator_3 (
    .Input1(in_1[13]), .Input2(in_2[13]), .great_in(fullcomparator_2_great_out),
    .less_in(fullcomparator_2_less_out), .equal_in(fullcomparator_2_equal_out),
    .great_out(fullcomparator_3_great_out), .less_out(fullcomparator_3_less_out),
    .equal_out(fullcomparator_3_equal_out));
  FullComparator fullcomparator_4 (
    .Input1(in_1[12]), .Input2(in_2[12]), .great_in(fullcomparator_3_great_out),
    .less_in(fullcomparator_3_less_out), .equal_in(fullcomparator_3_equal_out),
    .great_out(fullcomparator_4_great_out), .less_out(fullcomparator_4_less_out),
    .equal_out(fullcomparator_4_equal_out));
  FullComparator fullcomparator_5 (
    .Input1(in_1[11]), .Input2(in_2[11]), .great_in(fullcomparator_4_great_out),
    .less_in(fullcomparator_4_less_out), .equal_in(fullcomparator_4_equal_out),
    .great_out(fullcomparator_5_great_out), .less_out(fullcomparator_5_less_out),
    .equal_out(fullcomparator_5_equal_out));
  FullComparator fullcomparator_6 (
    .Input1(in_1[10]), .Input2(in_2[10]), .great_in(fullcomparator_5_great_out),
    .less_in(fullcomparator_5_less_out), .equal_in(fullcomparator_5_equal_out),
    .great_out(fullcomparator_6_great_out), .less_out(fullcomparator_6_less_out),
    .equal_out(fullcomparator_6_equal_out));
  FullComparator fullcomparator_7 (
    .Input1(in_1[9]), .Input2(in_2[9]), .great_in(fullcomparator_6_great_out),
    .less_in(fullcomparator_6_less_out), .equal_in(fullcomparator_6_equal_out),
    .great_out(fullcomparator_7_great_out), .less_out(fullcomparator_7_less_out),
    .equal_out(fullcomparator_7_equal_out));
  FullComparator fullcomparator_8 (
    .Input1(in_1[8]), .Input2(in_2[8]), .great_in(fullcomparator_7_great_out),
    .less_in(fullcomparator_7_less_out), .equal_in(fullcomparator_7_equal_out),
    .great_out(fullcomparator_8_great_out), .less_out(fullcomparator_8_less_out),
    .equal_out(fullcomparator_8_equal_out));
  FullComparator fullcomparator_9 (
    .Input1(in_1[7]), .Input2(in_2[7]), .great_in(fullcomparator_8_great_out),
    .less_in(fullcomparator_8_less_out), .equal_in(fullcomparator_8_equal_out),
    .great_out(fullcomparator_9_great_out), .less_out(fullcomparator_9_less_out),
    .equal_out(fullcomparator_9_equal_out));
  FullComparator fullcomparator_10 (
    .Input1(in_1[6]), .Input2(in_2[6]), .great_in(fullcomparator_9_great_out),
    .less_in(fullcomparator_9_less_out), .equal_in(fullcomparator_9_equal_out),
    .great_out(fullcomparator_10_great_out), .less_out(fullcomparator_10_less_out),
    .equal_out(fullcomparator_10_equal_out));
  FullComparator fullcomparator_11 (
    .Input1(in_1[5]), .Input2(in_2[5]), .great_in(fullcomparator_10_great_out),
    .less_in(fullcomparator_10_less_out), .equal_in(fullcomparator_10_equal_out),
    .great_out(fullcomparator_11_great_out), .less_out(fullcomparator_11_less_out),
    .equal_out(fullcomparator_11_equal_out));
  FullComparator fullcomparator_12 (
    .Input1(in_1[4]), .Input2(in_2[4]), .great_in(fullcomparator_11_great_out),
    .less_in(fullcomparator_11_less_out), .equal_in(fullcomparator_11_equal_out),
    .great_out(fullcomparator_12_great_out), .less_out(fullcomparator_12_less_out),
    .equal_out(fullcomparator_12_equal_out));
  FullComparator fullcomparator_13 (
    .Input1(in_1[3]), .Input2(in_2[3]), .great_in(fullcomparator_12_great_out),
    .less_in(fullcomparator_12_less_out), .equal_in(fullcomparator_12_equal_out),
    .great_out(fullcomparator_13_great_out), .less_out(fullcomparator_13_less_out),
    .equal_out(fullcomparator_13_equal_out));
  FullComparator fullcomparator_14 (
    .Input1(in_1[2]), .Input2(in_2[2]), .great_in(fullcomparator_13_great_out),
    .less_in(fullcomparator_13_less_out), .equal_in(fullcomparator_13_equal_out),
    .great_out(fullcomparator_14_great_out), .less_out(fullcomparator_14_less_out),
    .equal_out(fullcomparator_14_equal_out));
  FullComparator fullcomparator_15 (
    .Input1(in_1[1]), .Input2(in_2[1]), .great_in(fullcomparator_14_great_out),
    .less_in(fullcomparator_14_less_out), .equal_in(fullcomparator_14_equal_out),
    .great_out(fullcomparator_15_great_out), .less_out(fullcomparator_15_less_out),
    .equal_out(fullcomparator_15_equal_out));
  FullComparator fullcomparator_16 (
    .Input1(in_1[0]), .Input2(in_2[0]), .great_in(fullcomparator_15_great_out),
    .less_in(fullcomparator_15_less_out), .equal_in(fullcomparator_15_equal_out), .great_out(GreaterThan),
    .less_out(LessThan), .equal_out(Equal));
endmodule

// CompInstruction
module COMPInstruction (
  input  CompSignal,
  input  [15:0] OP1,
  input  [15:0] OP2,
  input  clock,
  output ZF,
  output CF
);

  wire and_1_out, and_2_out, comparator_1_equal, comparator_1_greaterthan, comparator_1_lessthan;

  Comparator comparator_1 (
    .in_1(OP1), .in_2(OP2), .GreaterThan(comparator_1_greaterthan), .LessThan(comparator_1_lessthan),
    .Equal(comparator_1_equal));
  and and_1 (and_1_out, ~comparator_1_greaterthan, ~comparator_1_lessthan, comparator_1_equal);  // AND_Gate
  and and_2 (and_2_out, ~comparator_1_greaterthan, comparator_1_lessthan, ~comparator_1_equal);  // AND_Gate
  Register #(.width(1)) register_1 (.D(and_1_out), .en(CompSignal), .Q(ZF), .clk(clock));  // open: clr
  Register #(.width(1)) register_2 (.D(and_2_out), .en(CompSignal), .Q(CF), .clk(clock));  // open: clr
endmodule

module ControlUnit (
  input  [15:0] Instruction,
  input  in_2,
  input  ZF,
  input  CF,
  output PcRead,
  output InstRead,
  output MemWrite,
  output MemRead,
  output [2:0] WriteReg,
  output [2:0] ReadReg2,
  output [2:0] ReadReg1,
  output [1:0] ALUControl,
  output PCWrite,
  output RegWrite,
  output CompSignal,
  output PcSelect
);

  wire and_1_out, and_2_out, and_3_out, and_4_out, and_5_out, and_6_out, decoder_1_out2, decoder_1_out3,
       decoder_1_out5, decoder_1_out6, decoder_1_out8, decoder_1_out9, decoder_1_out10, decoder_1_out11,
       decoder_1_out12, decoder_1_out13, not_1_out, or_1_out, or_2_out, or_3_out, or_6_out, or_7_out,
       register_1_q;
  wire [3:0] counter_1_q;

  Counter #(.width(4), .max('hf)) counter_1 (
    .load(InstRead), .D(Instruction[15:12]), .count(or_2_out), .Q(counter_1_q), .clk(in_2), .clr(and_1_out));  // open: carry
  and and_1 (and_1_out, not_1_out, register_1_q);
  not not_1 (not_1_out, or_2_out);
  Register #(.width(1)) register_1 (.D(or_1_out), .en(1'b1), .Q(register_1_q), .clk(in_2), .clr(1'b0));
  or or_1 (or_1_out, PCWrite, RegWrite);
  Decoder #(.select(4), .enable("false")) decoder_1 (
    .out0(PcRead), .out1(InstRead), .out2(decoder_1_out2), .out3(decoder_1_out3), .out5(decoder_1_out5),
    .out6(decoder_1_out6), .out7(CompSignal), .out8(decoder_1_out8), .out9(decoder_1_out9),
    .out10(decoder_1_out10), .out11(decoder_1_out11), .out12(decoder_1_out12), .out13(decoder_1_out13),
    .out14(MemRead), .out15(MemWrite), .sel(counter_1_q));  // open: out4
  or or_2 (or_2_out, PcRead, MemRead);
  or or_3 (or_3_out, ZF, CF);
  and and_2 (and_2_out, ZF, ~CF, decoder_1_out9);  // AND_Gate
  and and_3 (and_3_out, ~ZF, ~CF, decoder_1_out10);  // AND_Gate
  and and_4 (and_4_out, ~ZF, CF, decoder_1_out11);  // AND_Gate
  and and_5 (and_5_out, or_3_out, decoder_1_out12);
  and and_6 (and_6_out, ~CF, decoder_1_out13);  // AND_Gate
  or or_4 (RegWrite, decoder_1_out2, decoder_1_out3, decoder_1_out5, decoder_1_out6, MemRead);
  or or_5 (PcSelect, decoder_1_out8, and_2_out, and_3_out, and_4_out, and_5_out, and_6_out);
  or or_6 (or_6_out, decoder_1_out2, decoder_1_out6);
  or or_7 (or_7_out, decoder_1_out5, decoder_1_out3);
  or or_8 (ALUControl[1], decoder_1_out5, decoder_1_out6);
  or or_9 (PCWrite, decoder_1_out6, MemWrite, MemRead, decoder_1_out13, decoder_1_out12, decoder_1_out11, CompSignal, decoder_1_out10, decoder_1_out9, decoder_1_out8, decoder_1_out2, decoder_1_out3, decoder_1_out5);
  or or_10 (ALUControl[0], ~or_6_out, or_7_out);  // OR_Gate

  assign ReadReg1 = Instruction[11:9];
  assign ReadReg2 = Instruction[8:6];
  assign WriteReg = Instruction[5:3];

  // Notes on the sheet:
  //   Fetch1
  //   Fetch2
  //   AND
  //   ADD
  //   ADDI
  //   ANDI
  //   CMP
  //   JUMP
  //   JE
  //   JA
  //   JB
  //   JBE
  //   JAE
  //   LD
  //   ST
endmodule
